# Fritzing sketch blynk_leds_button (saved by Fritzing 0.9.3b)
breadboards: 1

parts:
  S1 = Pushbutton [package="[THT]"]
  Componente1 = Arduino Uno (Rev3)
  R1 = Resistor [tolerance=±5% resistance=10k package=THT]
  R4 = Resistor [tolerance=±5% resistance=220 package=THT]
  R5 = Resistor [tolerance=±5% resistance=220 package=THT]
  LED4 = LED - 5mm [color="White (8000K)" package="5 mm [THT]"]
  LED5 = LED - 5mm [color="Yellow (595nm)" package="5 mm [THT]"]
  LED6 = LED - 5mm [color="Red (633nm)" package="5 mm [THT]"]
  R6 = Resistor [tolerance=±5% resistance=220 package=THT]

nets:
  N1: S1.Pin_1, S1.Pin_2, Componente1.5V
  N2: S1.Pin_3, S1.Pin_4, Componente1.D3_PWM, R1.Pin_1
  N3: Componente1.D8, LED6.anode
  N4: Componente1.D6_PWM, LED5.anode
  N5: Componente1.D7, LED4.anode
  N6: R1.Pin_0, R4.Pin_1, R5.Pin_1
  N7: R4.Pin_0, LED6.cathode
  N8: R5.Pin_0, LED5.cathode
  N9: LED4.cathode, R6.Pin_0

// code stored in the sketch: blynk_leds_button.ino
/*
   Blynk leds when push button
   Button launch action
   16/02/2018
   ©Jacin Montava
*/

byte pinled_1 = 8; // Red led
byte pinled_2 = 7; // White led
byte pinled_3 = 6; // Yellow led
int delayTime = 500;
int pinbutton = 3;

void setup() {
  Serial.begin(9600);
  pinMode(pinled_1, OUTPUT);
  pinMode(pinled_2, OUTPUT);
  pinMode(pinled_3, OUTPUT);
  pinMode(pinbutton, INPUT);
}

void loop() {
  boolean buttonState = digitalRead(pinbutton);

  Serial.print("Button state: ");
  Serial.println(buttonState);

  if(buttonState == 1) {
    launchBlynks();
  }
}

void launchBlynks() {
  sameTime_blynk();
  alternate_blynk();
  blynk_one_to_one();
}

void sameTime_blynk() {
  digitalWrite(pinled_1, HIGH);
  digitalWrite(pinled_2, HIGH);
  digitalWrite(pinled_3, HIGH);
  delay(delayTime);

  digitalWrite(pinled_1, LOW);
  digitalWrite(pinled_2, LOW);
  digitalWrite(pinled_3, LOW);
  delay(delayTime);
}

void alternate_blynk() {
  digitalWrite(pinled_1, HIGH);
  delay(delayTime);
  digitalWrite(pinled_1, LOW);

  digitalWrite(pinled_2, HIGH);
  delay(delayTime);
  digitalWrite(pinled_2, LOW);

  digitalWrite(pinled_3, HIGH);
  delay(delayTime);
  digitalWrite(pinled_3, LOW);
  delay(delayTime);
}

void blynk_one_to_one() {
  digitalWrite(pinled_1, HIGH);
  delay(delayTime);
  digitalWrite(pinled_1, LOW);
  delay(delayTime);

  digitalWrite(pinled_2, HIGH);
  delay(delayTime);
  digitalWrite(pinled_2, LOW);
  delay(delayTime);

  digitalWrite(pinled_3, HIGH);
  delay(delayTime);
  digitalWrite(pinled_3, LOW);
  delay(delayTime);
}
